# Fritzing sketch arduino_scheme (saved by Fritzing 0.9.3b)
breadboards: 1

parts:
  arduino_uno = Arduino Uno (Rev3)  # not connected
  Smart_Phone1 = Smart Phone - 1Sheeld App  # not connected
  1Sheeld = 1Sheeld
  R1 = Resistor [tolerance=±5% resistance=220 package=THT]
  LED1 = LED - 5mm [color="Green (560nm)" package="5 mm [THT]"]
  LED2 = LED - 5mm [color="Yellow (592nm)" package="5 mm [THT]"]
  LED3 = LED - 5mm [color="Red (635nm)" package="5 mm [THT]"]
  LED4 = LED - 5mm [color="Green (565nm)" package="5 mm [THT]"]
  R3 = Resistor [tolerance=±5% resistance=220 package=THT]
  R2 = Resistor [tolerance=±5% resistance=220 package=THT]
  R4 = Resistor [tolerance=±5% resistance=220 package=THT]

nets:
  N1: 1Sheeld.D9, LED4.cathode, R4.Pin_1
  N2: 1Sheeld.D10, LED3.anode
  N3: 1Sheeld.D11, LED2.anode
  N4: 1Sheeld.D12, LED1.anode
  N5: 1Sheeld.GND, R1.Pin_1, R2.Pin_1, R4.Pin_0
  N6: R1.Pin_0, LED1.cathode
  N7: LED2.cathode, R3.Pin_0
  N8: LED3.cathode, R2.Pin_0

custom parts:
  Smart Phone - 1Sheeld App: Android Smart Phone
  1Sheeld: 1Sheeld is a new easily configured shield for Arduino. It is connected to a mobile app that allow the usage of all of Android smartphones' capabilities such as LCD Screen, Gyroscope, Switches, LEDs, Accelerometer, Magnetometer, GSM, Wi-Fi, GPS ...etc. into your Arduino sketch.

// code stored in the sketch: sms_button.ino
/*
SMS_button
Envoie un SMS et allume une LED en appuyant sur un bouton.
*/

#define CUSTOM_SETTINGS
#define INCLUDE_SMS_SHIELD

#include <OneSheeld.h>// Include 1Sheeld library.


//Constants
const int buttonPin = 8;     
const int ledPin =  9;
String phoneNumber = "123456789";
String phoneMessage = "Test from Arduino"; 

//Variables
int buttonState = 0;
int flag=0;

void setup() {
	
	OneSheeld.begin(); // Start communication
	
  	pinMode(ledPin, OUTPUT); //OV ou 5V      
  	pinMode(buttonPin, INPUT); //<3V ou >3V   
}

void loop() {
  //Read button state (pressed or not pressed?)
  buttonState = digitalRead(buttonPin);

  //If button pressed...
  if (buttonState == HIGH) { 
  	if(flag==0) {
      digitalWrite(ledPin, HIGH);
      SMS.send(phoneNumber,phoneMessage);
      flag = 1;
  	}
  }
    //...twice, turn led off!
  else if (buttonState == LOW) {
  	if (flag==1) {
      digitalWrite(ledPin, LOW);
      flag = 0;
  	}
  }   
    
  delay(200); //Small delay
}
